# Fritzing sketch Ir3 (saved by Fritzing 0.9.3b)
circuit board: 2.30618cm x 2.23563cm
breadboards: 1

parts:
  LED3 = LED - 5mm [color="Infrared (940nm)" package="5 mm [THT]"]
  LED4 = LED - 5mm [color="Infrared (940nm)" package="5 mm [THT]"]
  LED5 = LED - 5mm [color="Infrared (940nm)" package="5 mm [THT]"]
  R1 = Resistor [tolerance=±5% resistance=10 package=THT]
  Q1 = MOSFET-NCHANNEL [package=to220v]
  R5 = Resistor [tolerance=±5% resistance=100 package=THT]
  LED2 = LED - 5mm [color="Infrared (940nm)" package="5 mm [THT]"]
  R2 = Resistor [tolerance=±5% resistance=10 package=THT]
  Raspberry_Pi_1 = Raspberry Pi 3 [part_number=RPI-3-V1.2]
  R4 = Resistor [tolerance=±5% resistance=10k package=THT]
  IR2 = OSRB38C9AA
  LED1 = LED - 5mm [color="Red (633nm)" package="5 mm [THT]"]

nets:
  N1: LED3.cathode, Q1.D, LED2.cathode
  N2: LED3.anode, LED5.cathode
  N3: LED4.cathode, LED2.anode
  N4: LED4.anode, R1.Pin_0
  N5: LED5.anode, R2.Pin_0
  N6: R1.Pin_1, R2.Pin_1, Raspberry_Pi_1.5V
  N7: Q1.G, R4.Pin_1, LED1.cathode
  GND: Q1.S, Raspberry_Pi_1.GND, R4.Pin_0, IR2.GND
  N8: R5.Pin_0, LED1.anode
  N9: R5.Pin_1, Raspberry_Pi_1.GPIO27
  N10: Raspberry_Pi_1.GPIO22, IR2.OUT
  3V3: Raspberry_Pi_1.3V3, IR2.VCC

custom parts:
  OSRB38C9AA: 7..4*6..2*5..25mm Infrared Receiiver Modulle
