# Fritzing sketch Ir4b (saved by Fritzing 0.9.3b)
circuit board: 2.21121cm x 1.91175cm
breadboards: 1

parts:
  LED3 = LED - 5mm [color="Infrared (940nm)" package="5 mm [THT]"]
  LED4 = LED - 5mm [color="Infrared (940nm)" package="5 mm [THT]"]
  LED5 = LED - 5mm [color="Infrared (940nm)" package="5 mm [THT]"]
  R1 = Resistor [tolerance=±5% resistance=100 package=THT]
  R5 = Resistor [tolerance=±5% resistance=100 package=THT]
  LED2 = LED - 5mm [color="Infrared (940nm)" package="5 mm [THT]"]
  R2 = Resistor [tolerance=±5% resistance=100 package=THT]
  Raspberry_Pi_1 = Raspberry Pi 3 [part_number=RPI-3-V1.2]
  R4 = Resistor [tolerance=±5% resistance=10k package=THT]
  Q1 = MOSFET-NCHANNEL [part_number=2SK4017 package=to220v]
  R7 = Resistor [tolerance=±5% resistance=100 package=THT]
  IrR1 = OSRB38C9AA
  LED1 = LED - 3mm [color="Red (633nm)" package="3 mm [THT]"]

nets:
  N1: LED3.cathode, LED2.cathode, Q1.D
  N2: LED3.anode, LED5.cathode
  N3: LED4.cathode, LED2.anode
  N4: LED4.anode, R1.Pin_0
  N5: LED5.anode, R2.Pin_0
  N6: R1.Pin_1, R2.Pin_1, Raspberry_Pi_1.5V
  N7: R5.Pin_0, R4.Pin_1, Q1.G
  N8: R5.Pin_1, Raspberry_Pi_1.GPIO22, LED1.anode
  N9: Raspberry_Pi_1.GPIO27, IrR1.OUT
  3V3: Raspberry_Pi_1.3V3, IrR1.VCC
  GND: Raspberry_Pi_1.GND, R4.Pin_0, Q1.S, R7.Pin_1, IrR1.GND
  N10: R7.Pin_0, LED1.cathode

custom parts:
  OSRB38C9AA: 7..4*6..2*5..25mm Infrared Receiiver Modulle
