# Fritzing sketch Ir5 (saved by Fritzing 0.9.3b)
circuit board: 5.29103cm x 3.12258cm
breadboards: 1

parts:
  R2 = Resistor [tolerance=±5% resistance=10 package=THT]
  R1 = Resistor [tolerance=±5% resistance=10 package=THT]
  Q2 = Basic FET N-Channel [package="TO220 [THT]"]
  R3 = Resistor [tolerance=±5% resistance=100k package=THT]
  R4 = Resistor [tolerance=±5% resistance=100 package=THT]
  J2 = male pin header, 2 pins [form="♂ (male)"]
  J1 = male pin header, 4 pins [form="♂ (male)"]
  R5 = Resistor [tolerance=±5% resistance=10 package=THT]
  IrR1 = OSRB38C9AA
  J3 = shrouded pin header, 12 pins [form="♂ (shrouded male)"]
  MCU1 = Raspberry Pi Zero
  Oled1 = OLED SSD1306
  LED1 = LED - 3mm [color="Infrared (940nm)" package="3 mm [THT]"]
  LED3 = LED - 3mm [color="Infrared (940nm)" package="3 mm [THT]"]
  LED4 = LED - 3mm [color="Infrared (940nm)" package="3 mm [THT]"]
  LED2 = LED - 3mm [color="Infrared (940nm)" package="3 mm [THT]"]
  LED5 = LED - 3mm [color="Red (633nm)" package="3 mm [THT]"]

nets:
  N1: R2.Pin_0, R1.Pin_0, J2.pin1, J3.pin12, MCU1.pin_2, MCU1.pin_4
  N2: R2.Pin_1, LED3.anode
  N3: R1.Pin_1, LED2.anode
  N4: Q2.gate, R3.Pin_0, R4.Pin_0, LED5.anode
  N5: Q2.drain, LED1.cathode, LED4.cathode
  GND: Q2.source, R3.Pin_1, J2.pin2, J1.pin1, R5.Pin_1, IrR1.GND, J3.pin5, MCU1.pin_6, MCU1.pin_9, MCU1.pin_30, MCU1.pin_34, Oled1.GND
  N6: R4.Pin_1, J3.pin4
  VCC: J1.pin2, IrR1.VCC, J3.pin1, MCU1.pin_1, Oled1.VCC
  N7: J1.pin3, J3.pin3, MCU1.pin_5, Oled1.SCL
  N8: J1.pin4, J3.pin2, MCU1.pin_3, Oled1.SDA
  N9: R5.Pin_0, LED5.cathode
  N10: IrR1.OUT, J3.pin6
  N11: LED1.anode, LED2.cathode
  N12: LED3.cathode, LED4.anode

custom parts:
  OSRB38C9AA: 7..4*6..2*5..25mm Infrared Receiiver Modulle
  OLED SSD1306: OLED powered by a SSD1306 driver over I2C interface.
