# Fritzing sketch Ir2 (saved by Fritzing 0.9.3b)
circuit board: 2.75667cm x 2.54833cm
breadboards: 1

parts:
  LED1 = LED - 5mm [color="Red (633nm)" package="5 mm [THT]"]
  LED3 = LED - 5mm [color="Infrared (940nm)" package="5 mm [THT]"]
  LED4 = LED - 5mm [color="Infrared (940nm)" package="5 mm [THT]"]
  LED5 = LED - 5mm [color="Infrared (940nm)" package="5 mm [THT]"]
  R3 = Resistor [tolerance=±5% resistance=10k package=THT]
  R1 = Resistor [tolerance=±5% resistance=10 package=THT]
  Q1 = MOSFET-NCHANNEL [package=to220v]
  R5 = Resistor [tolerance=±5% resistance=100 package=THT]
  LED2 = LED - 5mm [color="Infrared (940nm)" package="5 mm [THT]"]
  Irecv1 = OSRB38C9AA [package="TO92 [THT]"]
  R2 = Resistor [tolerance=±5% resistance=10 package=THT]
  Raspberry_Pi_1 = Raspberry Pi 3 [part_number=RPI-3-V1.2]
  R4 = Resistor [tolerance=±5% resistance=10k package=THT]

nets:
  N1: LED1.cathode, LED3.cathode, Q1.D, LED2.cathode
  N2: LED1.anode, R3.Pin_0
  N3: LED3.anode, LED5.cathode
  N4: LED4.cathode, LED2.anode
  N5: LED4.anode, R1.Pin_0
  N6: LED5.anode, R2.Pin_0
  N7: R3.Pin_1, R1.Pin_1, R2.Pin_1, Raspberry_Pi_1.5V
  N8: Q1.G, R5.Pin_0, R4.Pin_1
  GND: Q1.S, Irecv1.GND, Raspberry_Pi_1.GND, R4.Pin_0
  N9: R5.Pin_1, Raspberry_Pi_1.GPIO27
  N10: Irecv1.Out, Raspberry_Pi_1.GPIO22
  VCC: Irecv1.Vcc, Raspberry_Pi_1.3V3

custom parts:
  OSRB38C9AA: Infrared Receiiver Modulle
